# Fritzing sketch platform-driver-circuit (saved by Fritzing 0.9.3b)
circuit board: 7.6366cm x 8.13579cm
breadboards: 1

parts:
  ATmega328 = atmega328 [package=dip]
  C2 = Ceramic Capacitor [capacitance=10µF package="100 mil [THT, multilayer]"]
  R3 = Resistor [tolerance=±5% resistance=68 package=THT]
  debug_LED = LED - 5mm [color="Green (570nm)" package="5 mm [THT]"]
  U2 = Voltage Regulator - 3.3V [package="TO220 [THT]"]
  R4 = Resistor [tolerance=±5% resistance=10k package=THT]
  C3 = Ceramic Capacitor [capacitance=10µF package="100 mil [THT, multilayer]"]
  power_plug = Power plug
  ICSP = AVR ISP 6 Pin [package=2x3_lock]
  serial_header = FTDI_BASIC [package=ftdi_basic]
  power_LED = LED - 5mm [color="Red (633nm)" package="5 mm [THT]"]
  R6 = Resistor [tolerance=±5% resistance=68 package=THT]
  R1 = Resistor [tolerance=±5% resistance=10k package=THT]
  BigEasyDriver_inputs = female pin header, 10 pins [form="♀ (female)"]
  R7 = Resistor [tolerance=±5% resistance=0 package=THT]
  R8 = Resistor [tolerance=±5% resistance=0 package=THT]
  S1 = Toggle Switch [package=THT]
  S2 = Toggle Switch [package=THT]
  emergency = screw terminal, 2 pins
  power = Taiway 100-SP-X-T1 SPDT Miniature Toggle Switch [part_number=100-SP-X-T1-0-0-B1-M1 package=THT]
  lasers = screw terminal, 4 pins
  stepper_motor = screw terminal, 4 pins
  power_supply = female pin header, 2 pins [form="♀ (female)"]
  stepper_motor_outputs = female pin header, 4 pins [form="♀ (female)"]
  limit_switches = screw terminal, 4 pins
  R2 = Resistor [tolerance=±5% resistance=10k package=THT]

nets:
  reset: ATmega328.RESET, R4.Pin_1, ICSP.5, serial_header.2
  RX: ATmega328.D0_(RX), serial_header.5
  TX: ATmega328.D1_(TX), serial_header.4
  N1: ATmega328.D2, BigEasyDriver_inputs.pin2
  N2: ATmega328.D3_(PWM), BigEasyDriver_inputs.pin1
  N3: ATmega328.D4, BigEasyDriver_inputs.pin9
  3.3V: ATmega328.VCC, ATmega328.AVCC, C2.1, U2.output_voltage, ICSP.2, serial_header.3, power_LED.anode, S1.COM, S2.COM, limit_switches.pin1, limit_switches.pin4
  GND: ATmega328.GND, C2.0, debug_LED.cathode, U2.GND, R4.Pin_0, C3.0, power_plug.GND, ICSP.6, serial_header.1, serial_header.6, R6.Pin_1, R1.Pin_1, BigEasyDriver_inputs.pin3, lasers.pin2, lasers.pin3, power_supply.pin2, R2.Pin_1
  N4: ATmega328.D5_(PWM), BigEasyDriver_inputs.pin8
  N5: ATmega328.D6_(PWM), BigEasyDriver_inputs.pin7
  N6: ATmega328.D7, BigEasyDriver_inputs.pin10
  N7: ATmega328.D9_(PWM), R3.Pin_1
  MOSI: ATmega328.D11_(PWM), ICSP.4
  MISO: ATmega328.D12, ICSP.1
  SCK: ATmega328.D13, ICSP.3
  N8: ATmega328.A4, limit_switches.pin2, R2.Pin_0
  N9: ATmega328.A5, R1.Pin_0, limit_switches.pin3
  N10: R3.Pin_0, debug_LED.anode
  N11: U2.input_voltage, C3.1, power.L1
  9V: power_plug.VCC, emergency.pin1, power_supply.pin1
  N12: power_LED.cathode, R6.Pin_0
  N13: R7.Pin_0, lasers.pin1
  N14: R7.Pin_1, S1.L1
  N15: R8.Pin_0, lasers.pin4
  N16: R8.Pin_1, S2.L1
  N17: emergency.pin2, power.COM
  N18: stepper_motor.pin1, stepper_motor_outputs.pin1
  N19: stepper_motor.pin2, stepper_motor_outputs.pin2
  N20: stepper_motor.pin3, stepper_motor_outputs.pin3
  N21: stepper_motor.pin4, stepper_motor_outputs.pin4
